// Logisim project Seven Segment Displays.circ as structural Verilog: 1 circuit, main circuit main
module main (
  input  [6:0] in_1,
  input  [6:0] in_2,
  input  [6:0] in_3,
  input  [6:0] in_4
);

  _7_Segment_Display #(.active("false")) u_7_segment_display_1 (
    .g(in_1[0]), .f(in_1[1]), .a(in_1[6]), .b(in_1[5]), .e(in_1[2]), .d(in_1[3]), .c(in_1[4]), .dp(1'b1));
  _7_Segment_Display #(.active("false")) u_7_segment_display_2 (
    .g(in_2[0]), .f(in_2[1]), .a(in_2[6]), .b(in_2[5]), .e(in_2[2]), .d(in_2[3]), .c(in_2[4]), .dp(1'b1));
  _7_Segment_Display #(.active("false")) u_7_segment_display_3 (
    .g(in_3[0]), .f(in_3[1]), .a(in_3[6]), .b(in_3[5]), .e(in_3[2]), .d(in_3[3]), .c(in_3[4]), .dp(1'b1));
  _7_Segment_Display #(.active("false")) u_7_segment_display_4 (
    .g(in_4[0]), .f(in_4[1]), .a(in_4[6]), .b(in_4[5]), .e(in_4[2]), .d(in_4[3]), .c(in_4[4]), .dp(1'b1));

  // Notes on the sheet:
  //   THOUSANDS DIGIT
  //   HUNDREDS DIGIT
  //   TENS DIGIT
  //   UNITS DIGIT
endmodule
